# Fritzing sketch Esquema-Projeto_Integrado_1 (saved by Fritzing 0.9.10b)
breadboards: 1

parts:
  Componente2 = Arduino Uno (Rev3)
  S2 = Pushbutton [package="[THT]"]
  R10 = PHOTOCELL [package=photocell]
  LED6 = smd LED [color="Yellow (595nm)" package="1206 [SMD]"]
  LED7 = smd LED [color="Red (635nm)" package="1206 [SMD]"]
  LED8 = smd LED [color="Red (635nm)" package="1206 [SMD]"]
  LED9 = smd LED [color="Red (635nm)" package="1206 [SMD]"]
  LED10 = smd LED [color="Red (635nm)" package="1206 [SMD]"]
  R11 = Resistor [tolerance=±5% resistance=330 package="2010 [SMD]"]
  R12 = Resistor [tolerance=±5% resistance=330 package="2010 [SMD]"]
  R13 = Resistor [tolerance=±5% resistance=330 package="2010 [SMD]"]
  R14 = Resistor [tolerance=±5% resistance=220 package="2010 [SMD]"]
  R15 = Resistor [tolerance=±5% resistance=220 package="2010 [SMD]"]
  R16 = Resistor [tolerance=±5% resistance=330 package="2010 [SMD]"]
  R17 = Resistor [tolerance=±5% resistance=330 package="2010 [SMD]"]
  R18 = Resistor [tolerance=±5% resistance=10k package="2010 [SMD]"]
  J3 = Piezo Speaker
  J4 = Piezo Speaker
  J5 = Basic Servo

nets:
  N1: Componente2.A0, R10.P$1, R18.Pin_1
  N2: Componente2.D8, R14.Pin_0
  N3: Componente2.D9_PWM, LED8.anode
  N4: Componente2.D10_PWM/SS, S2.Pin_1, S2.Pin_2
  GND: Componente2.D12/MISO, Componente2.GND, S2.Pin_3, S2.Pin_4, R11.Pin_0, R12.Pin_0, R13.Pin_0, R16.Pin_0, R17.Pin_0, R18.Pin_0, J3.pin1, J4.pin1, J5.gnd
  N5: Componente2.D2, LED10.anode
  N6: Componente2.D3_PWM, LED9.anode
  N7: Componente2.D4, LED6.anode
  N8: Componente2.D6_PWM, R15.Pin_0
  N9: Componente2.D7, J5.pulse
  5V: Componente2.5V, R10.P$2, J5.vcc
  N10: LED6.cathode, R13.Pin_1
  N11: LED7.cathode, R11.Pin_1
  N12: LED8.cathode, R12.Pin_1
  N13: LED9.cathode, R16.Pin_1
  N14: LED10.cathode, R17.Pin_1
  N15: R14.Pin_1, J3.pin2
  N16: R15.Pin_1, J4.pin2

// code stored in the sketch: Projetos.ino
/**
  Iluminação de garagem automática
  ------------------------
  |  Sensor  |  Arduino  |
  |   VCC    |    5V     |
  |  Trig    |    4V     |
  |  Echo    |    A4     |
  |   GND    |    GND    |
  ------------------------
  @author Luis, Pedro, Lucas, Miqueias e Joao
*/
int sensorLDR = 700;
long sensor;
int oitava = 1;
float SE5 = 659.25;
float SC5 = 523.25;
int LED = 9;
int leitor;
#include <Servo.h>
Servo servo1;

void setup() {
  Serial.begin(9600);
  digitalWrite(13, HIGH);    //LEDs do interruptor
  pinMode(2, OUTPUT);
  pinMode(3, OUTPUT);
  pinMode(4, OUTPUT);
  pinMode(10, INPUT_PULLUP);  //Campainha
  pinMode(9, OUTPUT);        //LED
  pinMode(8, OUTPUT);        //Buzzer
  pinMode(12, OUTPUT);  
  pinMode(11, OUTPUT);
  pinMode(6, OUTPUT);        //Buzzer
  servo1.attach(7);
  servo1.write(0);
  
 }

void loop() {

bluetooth();
campainha();
sensorLuminosidade();

}

void bluetooth() {



  if (Serial.available()) {                //essa estrutura evita o acionamento indevido do led ou de outros dispostivos
    leitor = Serial.read();                //armazenando a tecla pressionada na variavel leitor
    if (leitor == '1') {                   //se tecla 1 for pressionada
      digitalWrite(12, !digitalRead(12));  //ele vai verificar se o dispositivo esta ativado ou desativado
    } else if (leitor == '2') {            //se tecla 4 for pressionada
      digitalWrite(11, !digitalRead(11));  //ele vai verificar se o dispositivo esta ativado ou desativado
    } else if (leitor == '3') {            //abrir garagem via bluetooth
      abrirg();
    } else if (leitor == '4') {            //fechar garagem via bluetooth        /3 FECHA /4 LED
      fecharg();
    }
  }  
}

void abrirg() {

      servo1.write(90);
      digitalWrite(3, LOW);
      digitalWrite(4, HIGH);
      tone(6, 262);
      delay(500);
      digitalWrite(3, HIGH);
      digitalWrite(4, LOW);
      noTone(6);
      delay(500);
      digitalWrite(3, LOW);
      digitalWrite(4, HIGH);
      tone(6, 262);
      delay(500);
      digitalWrite(3, HIGH);
      digitalWrite(4, LOW);
      noTone(6);
      delay(500);
      digitalWrite(3, LOW);
      digitalWrite(4, HIGH);
      tone(6, 262);
      delay(500);
      digitalWrite(3, HIGH);
      digitalWrite(4, LOW);
      noTone(6);
      delay(500);
      digitalWrite(3, LOW);
      digitalWrite(4, HIGH);
      tone(6, 262);
      delay(500);
      digitalWrite(3, HIGH);
      digitalWrite(4, LOW);
      noTone(6);
      delay(500);
      digitalWrite(3, LOW);
      digitalWrite(4, HIGH);
      tone(6, 262);
      delay(500);
      digitalWrite(4, LOW);
      noTone(6);
}

void fecharg() {
      servo1.write(0);
      digitalWrite(3, LOW);
      digitalWrite(4, HIGH);
      tone(6, 262);
      delay(500);
      digitalWrite(3, HIGH);
      digitalWrite(4, LOW);
      noTone(6);
      delay(500);
      digitalWrite(3, LOW);
      digitalWrite(4, HIGH);
      tone(6, 262);
      delay(500);
      digitalWrite(3, HIGH);
      digitalWrite(4, LOW);
      noTone(6);
      delay(500);
      digitalWrite(3, LOW);
      digitalWrite(4, HIGH);
      tone(6, 262);
      delay(500);
      digitalWrite(3, HIGH);
      digitalWrite(4, LOW);
      noTone(6);
      delay(500);
      digitalWrite(3, LOW);
      digitalWrite(4, HIGH);
      tone(6, 262);
      delay(500);
      digitalWrite(3, HIGH);
      digitalWrite(4, LOW);
      noTone(6);
      delay(500);
      digitalWrite(3, LOW);
      digitalWrite(4, HIGH);
      tone(6, 262);
      delay(500);
      digitalWrite(4, LOW);
      noTone(6);
}

void sensorLuminosidade() {
  
int sensorLDR = analogRead(A0);
if (sensorLDR > 500) {
    digitalWrite(2, LOW);
 } else {
    digitalWrite(2, HIGH);
 }
  
}

void campainha() {
int campainha = 8;
  
  int sw2 = digitalRead(10);

  if (sw2 == 0) {
    tone(campainha, SE5 * oitava);
    digitalWrite(LED, HIGH);
    delay(200);
    digitalWrite(LED, LOW);
    delay(200);
    digitalWrite(LED, HIGH);
    delay(200);
    tone(campainha, SC5 * oitava);
    digitalWrite(LED, LOW);
    delay(200);
    digitalWrite(LED, HIGH);
    delay(200);
    digitalWrite(LED, LOW);
    delay(200);
  } else {
    digitalWrite(LED, LOW);
    noTone(campainha);
  }
}
