# Fritzing sketch Fritzing_Casa (saved by Fritzing 0.9.10b)
breadboards: 1

parts:
  Componente1 = Arduino Uno (Rev3)
  R1 = Photocell (LDR) [package=THT]
  R2 = Resistor [tolerance=±5% power=0.25 resistance=10k package=THT]
  R3 = Resistor [tolerance=±5% power=0.25 resistance=330 package=THT]
  R4 = Resistor [tolerance=±5% power=0.25 resistance=330 package=THT]
  LED1 = LED - 5mm [color="White (6500K)" current=0.030 package="5 mm [THT]"]
  LED2 = LED - 5mm [color="Red (635nm)" current=0.030 package="5 mm [THT]"]
  LED3 = LED - 5mm [color="Yellow (585nm)" current=0.030 package="5 mm [THT]"]
  R5 = Resistor [tolerance=±5% power=0.25 resistance=330 package=THT]
  J1 = Piezo Speaker
  R6 = Resistor [tolerance=±5% power=0.25 resistance=220 package=THT]
  J2 = Piezo Speaker
  R7 = Resistor [tolerance=±5% power=0.25 resistance=220 package=THT]
  LED4 = LED - 5mm [color="White (6500K)" current=0.030 package="5 mm [THT]"]
  R8 = Resistor [tolerance=±5% power=0.25 resistance=330 package=THT]
  S1 = Pushbutton [package="[THT]"]
  LED5 = LED - 5mm [color="White (6500K)" current=0.030 package="5 mm [THT]"]
  R9 = Resistor [tolerance=±5% power=0.25 resistance=330 package=THT]
  LED6 = LED - 5mm [color="White (6500K)" current=0.030 package="5 mm [THT]"]
  R10 = Resistor [tolerance=±5% power=0.25 resistance=330 package=THT]
  S2 = Toggle Switch [package=THT]
  S3 = Toggle Switch [package=THT]
  S4 = Toggle Switch [package=THT]
  LED7 = LED - 5mm [color="White (6500K)" current=0.030 package="5 mm [THT]"]
  R11 = Resistor [tolerance=±5% power=0.25 resistance=330 package=THT]
  LED8 = LED - 5mm [color="White (6500K)" current=0.030 package="5 mm [THT]"]
  R12 = Resistor [tolerance=±5% power=0.25 resistance=330 package=THT]
  J3 = Basic Servo
  Componente2 = Bluetooth HC-05 Macho
  R13 = Resistor [tolerance=±5% power=0.25 resistance=2.2k package=THT]
  R14 = Resistor [tolerance=±5% power=0.25 resistance=1k package=THT]

nets:
  N1: Componente1.A0, R1.pin_0, R2.Pin_1
  N2: Componente1.D8, R7.Pin_1
  N3: Componente1.D9_PWM, LED4.anode
  N4: Componente1.D10_PWM/SS, S1.Pin_1, S1.Pin_2
  N5: Componente1.D11_PWM/MOSI, LED8.anode
  N6: Componente1.D12/MISO, LED5.anode
  N7: Componente1.D13/SCK, S2.L2, S4.COM
  GND: Componente1.GND, R2.Pin_0, R3.Pin_0, R4.Pin_0, R5.Pin_0, J1.pin1, J2.pin1, R8.Pin_0, S1.Pin_3, S1.Pin_4, R9.Pin_0, LED6.cathode, LED7.cathode, R12.Pin_0, J3.gnd, Componente2.GND, R13.Pin_0
  N8: Componente1.D0/RX, Componente2.TXD
  N9: Componente1.D1/TX, R14.Pin_1
  N10: Componente1.D2, LED1.anode
  N11: Componente1.D3_PWM, LED2.anode
  N12: Componente1.D4, LED3.anode
  N13: Componente1.D6_PWM, R6.Pin_1
  N14: Componente1.D7, J3.pulse
  VCC: Componente1.5V, R1.pin_1, J3.vcc, Componente2.VCC
  N15: R3.Pin_1, LED1.cathode
  N16: R4.Pin_1, LED2.cathode
  N17: LED3.cathode, R5.Pin_1
  N18: J1.pin2, R6.Pin_0
  N19: J2.pin2, R7.Pin_0
  N20: LED4.cathode, R8.Pin_1
  N21: LED5.cathode, R9.Pin_1
  N22: LED6.anode, R10.Pin_1
  N23: R10.Pin_0, S2.COM
  N24: S3.L1, S4.L1
  N25: S3.COM, R11.Pin_1
  N26: S3.L2, S4.L2
  N27: LED7.anode, R11.Pin_0
  N28: LED8.cathode, R12.Pin_1
  N29: Componente2.RXD, R13.Pin_1, R14.Pin_0
